# Fritzing sketch home_module (saved by Fritzing 0.8.7b)
breadboards: 1

parts:
  Eleman1 = Arduino Uno (Rev3)
  part = ESP8266 WiFi Module [part_number=ESP8266]
  NRF24L1 = NRF24L01
  VCC1 = Battery
  LED1 = LED - 5mm [color="Red (633nm)" package="5 mm [THT]"]
  LED2 = LED - 5mm [color="Red (633nm)" package="5 mm [THT]"]
  LED3 = LED - 5mm [color="Red (633nm)" package="5 mm [THT]"]
  R1 = Resistor [tolerance=±5% resistance=220 package=THT]
  R2 = Resistor [tolerance=±5% resistance=220 package=THT]
  R3 = Resistor [tolerance=±5% resistance=220 package=THT]

nets:
  N1: Eleman1.D8, LED3.anode
  N2: Eleman1.D9_PWM, NRF24L1.CE
  N3: Eleman1.D10_PWM/SS, NRF24L1.CSN
  N4: Eleman1.D11_PWM/MOSI, NRF24L1.MOSI
  N5: Eleman1.D12/MISO, NRF24L1.MISO
  N6: Eleman1.D13/SCK, NRF24L1.SCK
  VCC: Eleman1.D0/RX, Eleman1.3V3, part.VCC, part.RST, part.CH_PD, part.TXD, NRF24L1.VCC
  GND: Eleman1.D1/TX, Eleman1.GND, part.RXD, part.GPIO_0, part.GPIO_2, part.GND, NRF24L1.GND, VCC1.-, R1.Pin_0, R2.Pin_0, R3.Pin_0
  N7: Eleman1.D3_PWM, LED2.anode
  N8: Eleman1.D4, LED1.anode
  N9: Eleman1.VIN, VCC1.+
  N10: LED1.cathode, R1.Pin_1
  N11: LED2.cathode, R2.Pin_1

custom parts:
  ESP8266 WiFi Module: Generic WiFi Module based on the ESP8266 with onboard PCB antenna and UART communications
  NRF24L01: NRF24L01 module
