# Fritzing sketch sub_module (saved by Fritzing 0.8.7b)
breadboards: 1

parts:
  Eleman1 = Arduino Uno (Rev3)
  NRF24L1 = NRF24L01
  VCC1 = Battery
  LED3 = LED - 5mm [color="Red (633nm)" package="5 mm [THT]"]
  R3 = Resistor [tolerance=±5% resistance=220 package=THT]
  KY-1 = Keyes Relay [package=THT]
  U1 = POT_SWITCH [package=pot_pth_switch]

nets:
  N1: Eleman1.A0, U1.G$2_1
  N2: Eleman1.D8, LED3.anode
  N3: Eleman1.D9_PWM, NRF24L1.CE
  N4: Eleman1.D10_PWM/SS, NRF24L1.CSN
  N5: Eleman1.D11_PWM/MOSI, NRF24L1.MOSI
  N6: Eleman1.D12/MISO, NRF24L1.MISO
  N7: Eleman1.D13/SCK, NRF24L1.SCK
  N8: Eleman1.D7, KY-1.signal
  3V3: Eleman1.3V3, NRF24L1.VCC, KY-1.power, U1.G$2_2
  GND: Eleman1.GND, NRF24L1.GND, VCC1.-, R3.Pin_0, KY-1.ground, U1.G$1_A
  N9: Eleman1.VIN, VCC1.+

custom parts:
  NRF24L01: NRF24L01 module
  Keyes Relay: The Keyes 5V relay module is suitable for SCM development, home appliance control. It uses a 5V~12V TIL control signal which can control DC / AC signal.
